# Fritzing sketch layout (saved by Fritzing 0.9.2b)
breadboards: 1

parts:
  Part1 = Adafruit Feather HUZZAH ESP8266 [part_number="Adafruit #2821"]
  S1 = Toggle Switch [package=THT]  # not connected
  S2 = Toggle Switch [package=THT]  # not connected

nets:
  N1: Part1.RESET, Part1.GPIO16

notes:
  4.3inch e-paper display
  blue and white wires not connected
  3-step toggle switches
  (4 pins each)

custom parts:
  Adafruit Feather HUZZAH ESP8266: his is the Adafruit Feather HUZZAH ESP8266 - our take on an 'all-in-one' ESP8266 WiFi development board with built in USB and battery charging. Its an ESP8266 WiFi module with all the extras you need, ready to rock! We have other boards in the Feather family, check'em out here. At the Feather HUZZAH's heart is an ESP8266 WiFi microcontroller clocked at 80 MHz and at 3.3V logic. This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
